# Fritzing sketch led2 (saved by Fritzing 0.9.4)
breadboards: 1

parts:
  R1 = Resistor [tolerance=±5% resistance=220 package=THT]
  LED1 = LED - 5mm [color="Red (633nm)" package="5 mm [THT]"]
  Part2 = Arduino Prototyping Shield
  R2 = Resistor [tolerance=±5% resistance=220 package=THT]
  LED2 = LED - 5mm [color="Red (633nm)" package="5 mm [THT]"]

nets:
  N1: R1.Pin_0, Part2.D8
  N2: R1.Pin_1, LED1.anode
  N3: LED1.cathode, Part2.GND, LED2.cathode
  N4: Part2.D12, R2.Pin_0
  N5: R2.Pin_1, LED2.anode

// code stored in the sketch: led1.ino
int led = 8;
int led1= 12;

void setup () {
    pinMode ( led, OUTPUT);
    pinMode (led1, OUTPUT);
}

void loop() {
    digitalWrite(led , HIGH);
    delay(1000);
    digitalWrite( led,LOW);
    delay(1000);
    digitalWrite (led1,HIGH);
    delay(1000);
    digitalWrite(led1,LOW);
    delay(1000);
}
